// Logisim project 加法器.circ as structural Verilog: 5 circuits, main circuit 半加器
module \半加器  (
  input  A,
  input  B,
  output S,
  output C
);

  xor xor_1 (S, A, B);
  and and_1 (C, A, B);
endmodule

module \全加器  (
  input  A,
  input  B,
  input  Ci,
  output S,
  output C
);

  wire nand_1_out, nand_2_out, xor_1_out;

  xor xor_1 (xor_1_out, A, B);
  xor xor_2 (S, xor_1_out, Ci);
  nand nand_1 (nand_1_out, xor_1_out, Ci);
  nand nand_2 (nand_2_out, A, B);
  nand nand_3 (C, nand_1_out, nand_2_out);
endmodule

module \串行加法器  (
  input  C0,
  input  A0,
  input  B0,
  input  A1,
  input  B1,
  input  A2,
  input  B2,
  input  A3,
  input  B3,
  output S0,
  output S1,
  output S2,
  output S3,
  output C4
);

  wire \全加器_1_c , \全加器_2_c , \全加器_3_c ;

  \全加器  \u_全加器_1  (.A(A0), .B(B0), .Ci(C0), .S(S0), .C(\全加器_1_c ));
  \全加器  \u_全加器_2  (.A(A1), .B(B1), .Ci(\全加器_1_c ), .S(S1), .C(\全加器_2_c ));
  \全加器  \u_全加器_3  (.A(A2), .B(B2), .Ci(\全加器_2_c ), .S(S2), .C(\全加器_3_c ));
  \全加器  \u_全加器_4  (.A(A3), .B(B3), .Ci(\全加器_3_c ), .S(S3), .C(C4));
endmodule

module \先行进位的加法器  (
  input  C0,
  input  A0,
  input  B0,
  input  A1,
  input  B1,
  input  A2,
  input  B2,
  input  A3,
  input  B3,
  output S0,
  output S1,
  output S2,
  output S3,
  output C4
);

  wire and_1_out, and_2_out, and_3_out, and_4_out, and_5_out, and_6_out, and_7_out, and_8_out, and_9_out,
       and_10_out, C1_out, C2_out, C3_out, G1_out, G2_out, G3_out, G4_out, P1_out, P2_out, P3_out, P4_out;

  xor P1 (P1_out, A0, B0);
  and G1 (G1_out, A0, B0);
  xor P2 (P2_out, A1, B1);
  and G2 (G2_out, A1, B1);
  xor P3 (P3_out, A2, B2);
  and G3 (G3_out, A2, B2);
  xor P4 (P4_out, A3, B3);
  and G4 (G4_out, A3, B3);
  and and_1 (and_1_out, C0, P1_out);
  and and_2 (and_2_out, C0, P1_out, P2_out);
  and and_3 (and_3_out, P2_out, G1_out);
  and and_4 (and_4_out, C0, P1_out, P2_out, P3_out);
  and and_5 (and_5_out, G1_out, P2_out, P3_out);
  and and_6 (and_6_out, P3_out, G2_out);
  and and_7 (and_7_out, C0, P1_out, P2_out, P3_out, P4_out);
  and and_8 (and_8_out, P4_out, P3_out, P2_out, G1_out);
  and and_9 (and_9_out, G2_out, P4_out, P3_out);
  and and_10 (and_10_out, G3_out, P4_out);
  or C1 (C1_out, and_1_out, G1_out);
  or C2 (C2_out, and_2_out, and_3_out, G2_out);
  or C3 (C3_out, and_4_out, and_5_out, G3_out, and_6_out);
  or u_C4 (C4, G4_out, and_7_out, and_8_out, and_9_out, and_10_out);
  xor F1 (S0, C0, P1_out);
  xor F2 (S1, C1_out, P2_out);
  xor F3 (S2, C2_out, P3_out);
  xor F4 (S3, P4_out, C3_out);
endmodule

module \先行进位加法器测试电路  (
  input  C0,
  input  A3,
  input  A2,
  input  A1,
  input  A0,
  input  B3,
  input  B2,
  input  B1,
  input  B0,
  output S3,
  output S2,
  output S1,
  output S0,
  output C4
);

  \先行进位的加法器  \u_先行进位的加法器_1  (
    .C0(C0), .A0(A0), .B0(B0), .A1(A1), .B1(B1), .A2(A2), .B2(B2), .A3(A3), .B3(B3), .S0(S0), .S1(S1),
    .S2(S2), .S3(S3), .C4(C4));
endmodule
