// Logisim project 门禁电路.circ as structural Verilog: 12 circuits, main circuit 四位二进制可逆计数器
module \四位二进制可逆计数器  (
  input  CPD,
  input  CPU,
  input  CLR,
  output QD,
  output QC,
  output QB,
  output QA
);

  wire and_1_out, and_2_out, and_3_out, and_4_out, and_5_out, and_6_out, d_ff_1_qn, d_ff_2_qn, d_ff_3_qn,
       d_ff_4_qn, or_1_out, or_2_out, or_3_out, or_4_out;

  and and_1 (and_1_out, d_ff_2_qn, d_ff_3_qn, d_ff_4_qn, CPD);
  and and_2 (and_2_out, QC, QB, QA, CPU);
  and and_3 (and_3_out, d_ff_3_qn, d_ff_4_qn, CPD);
  and and_4 (and_4_out, QB, QA, CPU);
  and and_5 (and_5_out, d_ff_4_qn, CPD);
  and and_6 (and_6_out, QA, CPU);
  or or_1 (or_1_out, and_1_out, and_2_out);
  or or_2 (or_2_out, and_3_out, and_4_out);
  or or_3 (or_3_out, and_5_out, and_6_out);
  or or_4 (or_4_out, CPD, CPU);
  D_Flip_Flop #(.trigger("falling")) d_ff_1 (
    .clk(or_1_out), .D(d_ff_1_qn), .Q(QD), .Qn(d_ff_1_qn), .reset(CLR));  // open: preset, en
  D_Flip_Flop #(.trigger("falling")) d_ff_2 (
    .clk(or_2_out), .D(d_ff_2_qn), .Q(QC), .Qn(d_ff_2_qn), .reset(CLR));  // open: preset, en
  D_Flip_Flop #(.trigger("falling")) d_ff_3 (
    .clk(or_3_out), .D(d_ff_3_qn), .Q(QB), .Qn(d_ff_3_qn), .reset(CLR));  // open: preset, en
  D_Flip_Flop #(.trigger("falling")) d_ff_4 (
    .clk(or_4_out), .D(d_ff_4_qn), .Q(QA), .Qn(d_ff_4_qn), .reset(CLR));  // open: preset, en
endmodule

module \四位二进制计数器测试电路  (
  input  CPU,
  input  CLR,
  input  CPD,
  output QD,
  output QC,
  output QB,
  output QA
);

  \四位二进制可逆计数器  \u_四位二进制可逆计数器_1  (.CPD(CPD), .CPU(CPU), .QD(QD), .QC(QC), .QB(QB), .QA(QA), .CLR(CLR));
endmodule

module \二进制转8421码  (
  input  A3,
  input  A2,
  input  A1,
  input  A0,
  output T3,
  output T2,
  output T1,
  output T0,
  output S3,
  output S2,
  output S1,
  output S0
);

  wire and_1_out, and_2_out, or_1_out;

  and and_1 (and_1_out, A3, A2);
  and and_2 (and_2_out, A3, A1);
  or or_1 (or_1_out, and_1_out, and_2_out);
  \先行进位的加法器  \u_先行进位的加法器_1  (
    .C0(1'b0), .A0(A0), .B0(1'b0), .A1(A1), .B1(or_1_out), .A2(A2), .B2(or_1_out), .A3(A3), .B3(1'b0),
    .S0(S0), .S1(S1), .S2(S2), .S3(S3), .C4(T0));

  assign T1 = 1'b0;
  assign T2 = 1'b0;
  assign T3 = 1'b0;

  // Notes on the sheet:
  //   十位数显示
  //   个位数显示
endmodule

module \二进制转8421码测试电路  (
  input  A3,
  input  A2,
  input  A1,
  input  A0,
  output T3,
  output T2,
  output T1,
  output T0,
  output S3,
  output S2,
  output S1,
  output S0
);

  \二进制转8421码  \u_二进制转8421码_1  (
    .A3(A3), .A2(A2), .A1(A1), .A0(A0), .T3(T3), .T2(T2), .T1(T1), .T0(T0), .S3(S3), .S2(S2), .S1(S1), .S0(S0));
endmodule

module \_7段译码电路  (
  input  A0,
  input  A1,
  input  A2,
  input  A3,
  output a,
  output b,
  output c,
  output d,
  output e,
  output f,
  output f_2
);

  wire A1_nA0_out, A2_A1_nA0_out, A2_nA1_A0_out, A2_nA1_out, A2A0_out, A3_nA1_nA0_out, nA1_nA0_out,
       nA2_nA1_nA0_2_out, nA2_nA1_nA0_out, nA3_A1_A0_out, nA3_A2_nA1_A0_out, nA3_A2_out, nA3_nA2_A1_out,
       nA3_nA2_nA1_out, nA3_nA2_out, not_1_out, not_2_out, not_3_out, not_4_out;

  not not_1 (not_1_out, A0);
  not not_2 (not_2_out, A1);
  not not_3 (not_3_out, A2);
  not not_4 (not_4_out, A3);
  and A2A0 (A2A0_out, A0, A2);
  and nA3_nA2_A1 (nA3_nA2_A1_out, not_4_out, A1, not_3_out);
  and nA2_nA1_nA0 (nA2_nA1_nA0_out, not_3_out, not_2_out, not_1_out);
  and nA1_nA0 (nA1_nA0_out, not_2_out, not_1_out);
  and nA3_nA2 (nA3_nA2_out, not_4_out, not_3_out);
  and nA3_A1_A0 (nA3_A1_A0_out, not_4_out, A1, A0);
  and nA3_A2 (nA3_A2_out, not_4_out, A2);
  and A3_nA1_nA0 (A3_nA1_nA0_out, not_2_out, not_1_out, A3);
  and nA2_nA1_nA0_2 (nA2_nA1_nA0_2_out, not_3_out, not_2_out, not_1_out);
  and nA3_A2_nA1_A0 (nA3_A2_nA1_A0_out, not_4_out, A2, not_2_out, A0);
  and A1_nA0 (A1_nA0_out, A1, not_1_out);
  and A2_nA1_A0 (A2_nA1_A0_out, A2, not_2_out, A0);
  and A2_A1_nA0 (A2_A1_nA0_out, A2, A1, not_1_out);
  and A2_nA1 (A2_nA1_out, A2, not_2_out);
  and nA3_nA2_nA1 (nA3_nA2_nA1_out, not_4_out, not_3_out, A1);
  or or_1 (a, A2A0_out, nA3_nA2_A1_out, nA2_nA1_nA0_out, A3);
  or or_2 (b, A3, nA1_nA0_out, nA3_nA2_out, nA3_A1_A0_out);
  or or_3 (c, A3, not_2_out, nA3_A2_out, nA3_A1_A0_out);
  or or_4 (d, A3_nA1_nA0_out, nA2_nA1_nA0_2_out, nA3_nA2_A1_out, nA3_A2_nA1_A0_out, A1_nA0_out);
  or or_5 (e, A3_nA1_nA0_out, nA2_nA1_nA0_2_out, A1_nA0_out);
  or or_6 (f, A3, nA1_nA0_out, A2_nA1_A0_out, A2_A1_nA0_out);
  or or_7 (f_2, A3, A2_nA1_out, A1_nA0_out, nA3_nA2_nA1_out);
endmodule

module \七段译码显示电路  (
  input  A3,
  input  A2,
  input  A1,
  input  A0
);

  wire \n7段译码电路_1_a , \n7段译码电路_1_b , \n7段译码电路_1_c , \n7段译码电路_1_d , \n7段译码电路_1_e , \n7段译码电路_1_f ,
       \n7段译码电路_1_f_2 ;

  _7_Segment_Display u_7_segment_display_1 (
    .g(\n7段译码电路_1_f_2 ), .f(\n7段译码电路_1_f ), .a(\n7段译码电路_1_a ), .b(\n7段译码电路_1_b ), .e(\n7段译码电路_1_e ),
    .d(\n7段译码电路_1_d ), .c(\n7段译码电路_1_c ));  // open: dp
  \_7段译码电路  \u_7段译码电路_1  (
    .A0(A0), .A1(A1), .A2(A2), .A3(A3), .a(\n7段译码电路_1_a ), .b(\n7段译码电路_1_b ), .c(\n7段译码电路_1_c ),
    .d(\n7段译码电路_1_d ), .e(\n7段译码电路_1_e ), .f(\n7段译码电路_1_f ), .f_2(\n7段译码电路_1_f_2 ));
endmodule

module \七段译码器显示人数  (
  input  QD,
  input  QC,
  input  QB,
  input  QA
);

  wire \n7段译码电路_1_a , \n7段译码电路_1_b , \n7段译码电路_1_c , \n7段译码电路_1_d , \n7段译码电路_1_e , \n7段译码电路_1_f ,
       \n7段译码电路_1_f_2 , \n7段译码电路_2_a , \n7段译码电路_2_b , \n7段译码电路_2_c , \n7段译码电路_2_d , \n7段译码电路_2_e ,
       \n7段译码电路_2_f , \n7段译码电路_2_f_2 , \二进制转8421码_1_s0 , \二进制转8421码_1_s1 , \二进制转8421码_1_s2 ,
       \二进制转8421码_1_s3 , \二进制转8421码_1_t0 , \二进制转8421码_1_t1 , \二进制转8421码_1_t2 , \二进制转8421码_1_t3 ;

  \_7段译码电路  \u_7段译码电路_1  (
    .A0(\二进制转8421码_1_t0 ), .A1(\二进制转8421码_1_t1 ), .A2(\二进制转8421码_1_t2 ), .A3(\二进制转8421码_1_t3 ),
    .a(\n7段译码电路_1_a ), .b(\n7段译码电路_1_b ), .c(\n7段译码电路_1_c ), .d(\n7段译码电路_1_d ), .e(\n7段译码电路_1_e ),
    .f(\n7段译码电路_1_f ), .f_2(\n7段译码电路_1_f_2 ));
  \二进制转8421码  \u_二进制转8421码_1  (
    .A3(QD), .A2(QC), .A1(QB), .A0(QA), .T3(\二进制转8421码_1_t3 ), .T2(\二进制转8421码_1_t2 ), .T1(\二进制转8421码_1_t1 ),
    .T0(\二进制转8421码_1_t0 ), .S3(\二进制转8421码_1_s3 ), .S2(\二进制转8421码_1_s2 ), .S1(\二进制转8421码_1_s1 ),
    .S0(\二进制转8421码_1_s0 ));
  _7_Segment_Display u_7_segment_display_1 (
    .g(\n7段译码电路_2_f_2 ), .f(\n7段译码电路_2_f ), .a(\n7段译码电路_2_a ), .b(\n7段译码电路_2_b ), .e(\n7段译码电路_2_e ),
    .d(\n7段译码电路_2_d ), .c(\n7段译码电路_2_c ));  // open: dp
  _7_Segment_Display u_7_segment_display_2 (
    .g(\n7段译码电路_1_f_2 ), .f(\n7段译码电路_1_f ), .a(\n7段译码电路_1_a ), .b(\n7段译码电路_1_b ), .e(\n7段译码电路_1_e ),
    .d(\n7段译码电路_1_d ), .c(\n7段译码电路_1_c ));  // open: dp
  \_7段译码电路  \u_7段译码电路_2  (
    .A0(\二进制转8421码_1_s0 ), .A1(\二进制转8421码_1_s1 ), .A2(\二进制转8421码_1_s2 ), .A3(\二进制转8421码_1_s3 ),
    .a(\n7段译码电路_2_a ), .b(\n7段译码电路_2_b ), .c(\n7段译码电路_2_c ), .d(\n7段译码电路_2_d ), .e(\n7段译码电路_2_e ),
    .f(\n7段译码电路_2_f ), .f_2(\n7段译码电路_2_f_2 ));
endmodule

module \报警电路  (
  input  CRL,
  input  UP,
  input  DOWN,
  output QD,
  output QC,
  output QB,
  output QA,
  output ALARM
);

  wire DEC_out, INC_out, nand_1_out, or_1_out;

  \四位二进制可逆计数器  \u_四位二进制可逆计数器_1  (.CPD(DEC_out), .CPU(INC_out), .QD(QD), .QC(QC), .QB(QB), .QA(QA), .CLR(CRL));
  and INC (INC_out, nand_1_out, UP);
  and DEC (DEC_out, or_1_out, DOWN);
  nand nand_1 (nand_1_out, QD, QC, QB, QA);
  or or_1 (or_1_out, QD, QC, QB, QA);
  and u_ALARM (ALARM, QD, QC, QB, QA, UP);
endmodule

module \报警电路测试电路  (
  input  UP,
  input  CLR,
  input  DOWN,
  output QD,
  output QC,
  output QB,
  output QA,
  output ALARM
);

  \报警电路  \u_报警电路_1  (.QD(QD), .QC(QC), .QB(QB), .QA(QA), .ALARM(ALARM), .CRL(CLR), .UP(UP), .DOWN(DOWN));
endmodule

module \小型实验室门禁系统电路  (
  input  UP,
  input  CLR,
  input  DOWN,
  output _1a,
  output _1b,
  output _1c,
  output _1d,
  output _1e,
  output _1f,
  output _1g,
  output _0a,
  output _0b,
  output _0c,
  output _0d,
  output _0e,
  output _0f,
  output _0g,
  output ALARM
);

  wire \二进制转8421码_1_s0 , \二进制转8421码_1_s1 , \二进制转8421码_1_s2 , \二进制转8421码_1_s3 , \二进制转8421码_1_t0 ,
       \二进制转8421码_1_t1 , \二进制转8421码_1_t2 , \二进制转8421码_1_t3 , \报警电路_1_qa , \报警电路_1_qb , \报警电路_1_qc ,
       \报警电路_1_qd ;

  \_7段译码电路  \u_7段译码电路_1  (
    .A0(\二进制转8421码_1_t0 ), .A1(\二进制转8421码_1_t1 ), .A2(\二进制转8421码_1_t2 ), .A3(\二进制转8421码_1_t3 ), .a(_1a),
    .b(_1b), .c(_1c), .d(_1d), .e(_1e), .f(_1f), .f_2(_1g));
  \二进制转8421码  \u_二进制转8421码_1  (
    .A3(\报警电路_1_qd ), .A2(\报警电路_1_qc ), .A1(\报警电路_1_qb ), .A0(\报警电路_1_qa ), .T3(\二进制转8421码_1_t3 ),
    .T2(\二进制转8421码_1_t2 ), .T1(\二进制转8421码_1_t1 ), .T0(\二进制转8421码_1_t0 ), .S3(\二进制转8421码_1_s3 ),
    .S2(\二进制转8421码_1_s2 ), .S1(\二进制转8421码_1_s1 ), .S0(\二进制转8421码_1_s0 ));
  \报警电路  \u_报警电路_1  (
    .QD(\报警电路_1_qd ), .QC(\报警电路_1_qc ), .QB(\报警电路_1_qb ), .QA(\报警电路_1_qa ), .ALARM(ALARM), .CRL(CLR),
    .UP(UP), .DOWN(DOWN));
  \_7段译码电路  \u_7段译码电路_2  (
    .A0(\二进制转8421码_1_s0 ), .A1(\二进制转8421码_1_s1 ), .A2(\二进制转8421码_1_s2 ), .A3(\二进制转8421码_1_s3 ), .a(_0a),
    .b(_0b), .c(_0c), .d(_0d), .e(_0e), .f(_0f), .f_2(_0g));
endmodule

module \门禁电路封装后  (
  input  in_1,
  input  in_2,
  input  in_3,
  output out_4,
  output out_5,
  output out_6,
  output out_7,
  output out_8,
  output out_9,
  output out_10,
  output out_11,
  output out_12,
  output out_13,
  output out_14,
  output out_15,
  output out_16,
  output out_17,
  output out_18
);

  \小型实验室门禁系统电路  \u_小型实验室门禁系统电路_1  (
    .ALARM(out_18), ._1a(out_4), ._1b(out_5), ._1c(out_6), ._1d(out_7), ._1e(out_8), ._1f(out_9),
    ._1g(out_10), ._0a(out_11), ._0b(out_12), ._0c(out_13), ._0d(out_14), ._0e(out_15), ._0f(out_16),
    ._0g(out_17), .UP(in_1), .CLR(in_2), .DOWN(in_3));
endmodule

module \最终带人数显示的门禁电路  (
  input  UP,
  input  CLR,
  input  DOWN,
  output ALARM
);

  wire \小型实验室门禁系统电路_1__0a , \小型实验室门禁系统电路_1__0b , \小型实验室门禁系统电路_1__0c , \小型实验室门禁系统电路_1__0d ,
       \小型实验室门禁系统电路_1__0e , \小型实验室门禁系统电路_1__0f , \小型实验室门禁系统电路_1__0g , \小型实验室门禁系统电路_1__1a ,
       \小型实验室门禁系统电路_1__1b , \小型实验室门禁系统电路_1__1c , \小型实验室门禁系统电路_1__1d , \小型实验室门禁系统电路_1__1e ,
       \小型实验室门禁系统电路_1__1f , \小型实验室门禁系统电路_1__1g ;

  \小型实验室门禁系统电路  \u_小型实验室门禁系统电路_1  (
    .ALARM(ALARM), ._1a(\小型实验室门禁系统电路_1__1a ), ._1b(\小型实验室门禁系统电路_1__1b ), ._1c(\小型实验室门禁系统电路_1__1c ),
    ._1d(\小型实验室门禁系统电路_1__1d ), ._1e(\小型实验室门禁系统电路_1__1e ), ._1f(\小型实验室门禁系统电路_1__1f ),
    ._1g(\小型实验室门禁系统电路_1__1g ), ._0a(\小型实验室门禁系统电路_1__0a ), ._0b(\小型实验室门禁系统电路_1__0b ),
    ._0c(\小型实验室门禁系统电路_1__0c ), ._0d(\小型实验室门禁系统电路_1__0d ), ._0e(\小型实验室门禁系统电路_1__0e ),
    ._0f(\小型实验室门禁系统电路_1__0f ), ._0g(\小型实验室门禁系统电路_1__0g ), .UP(UP), .CLR(CLR), .DOWN(DOWN));
  _7_Segment_Display u_7_segment_display_1 (
    .g(\小型实验室门禁系统电路_1__1g ), .f(\小型实验室门禁系统电路_1__1f ), .a(\小型实验室门禁系统电路_1__1a ), .b(\小型实验室门禁系统电路_1__1b ),
    .e(\小型实验室门禁系统电路_1__1e ), .d(\小型实验室门禁系统电路_1__1d ), .c(\小型实验室门禁系统电路_1__1c ));  // open: dp
  _7_Segment_Display u_7_segment_display_2 (
    .g(\小型实验室门禁系统电路_1__0g ), .f(\小型实验室门禁系统电路_1__0f ), .a(\小型实验室门禁系统电路_1__0a ), .b(\小型实验室门禁系统电路_1__0b ),
    .e(\小型实验室门禁系统电路_1__0e ), .d(\小型实验室门禁系统电路_1__0d ), .c(\小型实验室门禁系统电路_1__0c ));  // open: dp
endmodule
