// Logisim project 乘法器和除法器.circ as structural Verilog: 6 circuits, main circuit 4x4乘法器
module \_4x4乘法器  (
  input  [3:0] a_3_0,
  input  [3:0] b_3_0,
  output [7:0] p_7_0
);

  wire [7:0] adder_1_out, adder_2_out, adder_3_out, adder_4_out, multiplexer_1_out, multiplexer_2_out,
       multiplexer_3_out, shifter_1_out, shifter_2_out, shifter_3_out;

  Adder adder_1 (.a({8{1'b0}}), .b({4'b0000, b_3_0}), .out(adder_1_out));  // open: cin, cout
  Shifter shifter_1 (.in({4'b0000, b_3_0}), .\dist (3'b001), .out(shifter_1_out));
  Multiplexer #(.width(8)) multiplexer_1 (
    .in0({8{1'b0}}), .in1(adder_1_out), .out(multiplexer_1_out), .sel(a_3_0[0]));  // open: en
  Adder adder_2 (.a(multiplexer_1_out), .b(shifter_1_out), .out(adder_2_out));  // open: cin, cout
  Shifter shifter_2 (.in(shifter_1_out), .\dist (3'b001), .out(shifter_2_out));
  Multiplexer #(.width(8)) multiplexer_2 (
    .in0(multiplexer_1_out), .in1(adder_2_out), .out(multiplexer_2_out), .sel(a_3_0[1]));  // open: en
  Adder adder_3 (.a(multiplexer_2_out), .b(shifter_2_out), .out(adder_3_out));  // open: cin, cout
  Shifter shifter_3 (.in(shifter_2_out), .\dist (3'b001), .out(shifter_3_out));
  Multiplexer #(.width(8)) multiplexer_3 (
    .in0(multiplexer_2_out), .in1(adder_3_out), .out(multiplexer_3_out), .sel(a_3_0[2]));  // open: en
  Adder adder_4 (.a(multiplexer_3_out), .b(shifter_3_out), .out(adder_4_out));  // open: cin, cout
  Multiplexer #(.width(8)) multiplexer_4 (
    .in0(multiplexer_3_out), .in1(adder_4_out), .out(p_7_0), .sel(a_3_0[3]));  // open: en
  // Probe on p_7_0
endmodule

module \_32x4乘法器  (
  input  [3:0] a_3_0,
  input  [31:0] b_31_0,
  output [31:0] p_31_0
);

  wire [31:0] adder_1_out, adder_2_out, adder_3_out, adder_4_out, multiplexer_1_out, multiplexer_2_out,
       multiplexer_3_out, shifter_1_out, shifter_2_out, shifter_3_out;

  // Probe on b_31_0
  Adder #(.width(32)) adder_1 (.a({32{1'b0}}), .b(b_31_0), .out(adder_1_out));  // open: cin, cout
  Multiplexer #(.width(32)) multiplexer_1 (
    .in0({32{1'b0}}), .in1(adder_1_out), .out(multiplexer_1_out), .sel(a_3_0[0]));  // open: en
  Shifter #(.width(32)) shifter_1 (.in(b_31_0), .\dist (5'b00001), .out(shifter_1_out));
  Adder #(.width(32)) adder_2 (.a(multiplexer_1_out), .b(shifter_1_out), .out(adder_2_out));  // open: cin, cout
  Multiplexer #(.width(32)) multiplexer_2 (
    .in0(multiplexer_1_out), .in1(adder_2_out), .out(multiplexer_2_out), .sel(a_3_0[1]));  // open: en
  Shifter #(.width(32)) shifter_2 (.in(shifter_1_out), .\dist (5'b00001), .out(shifter_2_out));
  Adder #(.width(32)) adder_3 (.a(multiplexer_2_out), .b(shifter_2_out), .out(adder_3_out));  // open: cin, cout
  Multiplexer #(.width(32)) multiplexer_3 (
    .in0(multiplexer_2_out), .in1(adder_3_out), .out(multiplexer_3_out), .sel(a_3_0[2]));  // open: en
  Shifter #(.width(32)) shifter_3 (.in(shifter_2_out), .\dist (5'b00001), .out(shifter_3_out));
  Adder #(.width(32)) adder_4 (.a(multiplexer_3_out), .b(shifter_3_out), .out(adder_4_out));  // open: cin, cout
  Multiplexer #(.width(32)) multiplexer_4 (
    .in0(multiplexer_3_out), .in1(adder_4_out), .out(p_31_0), .sel(a_3_0[3]));  // open: en
  // Probe on p_31_0
endmodule

module \_32x32乘法器  (
  input  [31:0] a_31_0,
  input  [31:0] b_31_0,
  output [31:0] p_31_0
);

  wire [31:0] adder_1_out, adder_2_out, adder_3_out, adder_4_out, adder_5_out, adder_6_out,
       \n32x4乘法器_1_p_31_0 , \n32x4乘法器_2_p_31_0 , \n32x4乘法器_3_p_31_0 , \n32x4乘法器_4_p_31_0 ,
       \n32x4乘法器_5_p_31_0 , \n32x4乘法器_6_p_31_0 , \n32x4乘法器_7_p_31_0 , \n32x4乘法器_8_p_31_0 , shifter_1_out,
       shifter_2_out, shifter_3_out, shifter_4_out, shifter_5_out, shifter_6_out, shifter_7_out;

  // Probe on a_31_0
  // Probe on b_31_0
  \_32x4乘法器  \u_32x4乘法器_1  (.b_31_0(b_31_0), .p_31_0(\n32x4乘法器_1_p_31_0 ), .a_3_0(a_31_0[3:0]));
  \_32x4乘法器  \u_32x4乘法器_2  (.b_31_0(b_31_0), .p_31_0(\n32x4乘法器_2_p_31_0 ), .a_3_0(a_31_0[7:4]));
  \_32x4乘法器  \u_32x4乘法器_3  (.b_31_0(b_31_0), .p_31_0(\n32x4乘法器_3_p_31_0 ), .a_3_0(a_31_0[11:8]));
  \_32x4乘法器  \u_32x4乘法器_4  (.b_31_0(b_31_0), .p_31_0(\n32x4乘法器_4_p_31_0 ), .a_3_0(a_31_0[15:12]));
  \_32x4乘法器  \u_32x4乘法器_5  (.b_31_0(b_31_0), .p_31_0(\n32x4乘法器_5_p_31_0 ), .a_3_0(a_31_0[19:16]));
  \_32x4乘法器  \u_32x4乘法器_6  (.b_31_0(b_31_0), .p_31_0(\n32x4乘法器_6_p_31_0 ), .a_3_0(a_31_0[23:20]));
  \_32x4乘法器  \u_32x4乘法器_7  (.b_31_0(b_31_0), .p_31_0(\n32x4乘法器_7_p_31_0 ), .a_3_0(a_31_0[27:24]));
  \_32x4乘法器  \u_32x4乘法器_8  (.b_31_0(b_31_0), .p_31_0(\n32x4乘法器_8_p_31_0 ), .a_3_0(a_31_0[31:28]));
  Shifter #(.width(32)) shifter_1 (.in(\n32x4乘法器_2_p_31_0 ), .\dist (5'b00100), .out(shifter_1_out));
  Shifter #(.width(32)) shifter_2 (.in(\n32x4乘法器_3_p_31_0 ), .\dist (5'b01000), .out(shifter_2_out));
  Shifter #(.width(32)) shifter_3 (.in(\n32x4乘法器_4_p_31_0 ), .\dist (5'b01100), .out(shifter_3_out));
  Shifter #(.width(32)) shifter_4 (.in(\n32x4乘法器_5_p_31_0 ), .\dist (5'b10000), .out(shifter_4_out));
  Shifter #(.width(32)) shifter_5 (.in(\n32x4乘法器_6_p_31_0 ), .\dist (5'b10100), .out(shifter_5_out));
  Shifter #(.width(32)) shifter_6 (.in(\n32x4乘法器_7_p_31_0 ), .\dist (5'b11000), .out(shifter_6_out));
  Shifter #(.width(32)) shifter_7 (.in(\n32x4乘法器_8_p_31_0 ), .\dist (5'b11100), .out(shifter_7_out));
  Adder #(.width(32)) adder_1 (.a(\n32x4乘法器_1_p_31_0 ), .b(shifter_1_out), .out(adder_1_out));  // open: cin, cout
  Adder #(.width(32)) adder_2 (.a(shifter_2_out), .b(shifter_3_out), .out(adder_2_out));  // open: cin, cout
  Adder #(.width(32)) adder_3 (.a(shifter_4_out), .b(shifter_5_out), .out(adder_3_out));  // open: cin, cout
  Adder #(.width(32)) adder_4 (.a(shifter_6_out), .b(shifter_7_out), .out(adder_4_out));  // open: cin, cout
  Adder #(.width(32)) adder_5 (.a(adder_1_out), .b(adder_2_out), .out(adder_5_out));  // open: cin, cout
  Adder #(.width(32)) adder_6 (.a(adder_3_out), .b(adder_4_out), .out(adder_6_out));  // open: cin, cout
  Adder #(.width(32)) adder_7 (.a(adder_5_out), .b(adder_6_out), .out(p_31_0));  // open: cin, cout
  // Probe on p_31_0
endmodule

module \四位除法器  (
  input  [3:0] n2,
  input  [3:0] d,
  output [3:0] rem,
  output [3:0] quot
);

  wire comparator_1_eq, comparator_1_gt, comparator_2_eq, comparator_2_gt, comparator_3_eq, comparator_3_gt,
       comparator_4_eq, comparator_4_gt, or_2_out, or_4_out, or_6_out, or_8_out;
  wire [3:0] multiplexer_1_out, multiplexer_2_out, multiplexer_5_out, multiplexer_6_out, or_1_out, or_3_out,
       or_5_out, or_7_out, subtractor_1_out, subtractor_2_out, subtractor_3_out, subtractor_4_out;
  wire [7:0] multiplexer_4_out, shifter_1_out, shifter_2_out, shifter_3_out, shifter_4_out;

  Shifter shifter_1 (.in({4'b0000, n2}), .\dist (3'b001), .out(shifter_1_out));
  Comparator #(.width(4), .mode("unsigned")) comparator_1 (
    .a(shifter_1_out[7:4]), .b(d), .gt(comparator_1_gt), .eq(comparator_1_eq));  // open: lt
  Subtractor #(.width(4)) subtractor_1 (.a(shifter_1_out[7:4]), .b(d), .out(subtractor_1_out));  // open: bin, bout
  assign or_1_out = shifter_1_out[3:0] | 4'b0001;  // OR_Gate or_1, 4 bits wide
  or or_2 (or_2_out, comparator_1_gt, comparator_1_eq);
  Multiplexer #(.width(4)) multiplexer_1 (
    .in0(shifter_1_out[7:4]), .in1(subtractor_1_out), .out(multiplexer_1_out), .sel(or_2_out));  // open: en
  Multiplexer #(.width(4)) multiplexer_2 (
    .in0(shifter_1_out[3:0]), .in1(or_1_out), .out(multiplexer_2_out), .sel(or_2_out));  // open: en
  Shifter shifter_2 (.in({multiplexer_1_out, multiplexer_2_out}), .\dist (3'b001), .out(shifter_2_out));
  Comparator #(.width(4), .mode("unsigned")) comparator_2 (
    .a(shifter_2_out[7:4]), .b(d), .gt(comparator_2_gt), .eq(comparator_2_eq));  // open: lt
  Subtractor #(.width(4)) subtractor_2 (.a(shifter_2_out[7:4]), .b(d), .out(subtractor_2_out));  // open: bin, bout
  assign or_3_out = shifter_2_out[3:0] | 4'b0001;  // OR_Gate or_3, 4 bits wide
  or or_4 (or_4_out, comparator_2_gt, comparator_2_eq);
  Multiplexer #(.width(4)) multiplexer_3 (
    .in0(shifter_2_out[7:4]), .in1(subtractor_2_out), .out(multiplexer_4_out[7:4]), .sel(or_4_out));  // open: en
  Multiplexer #(.width(4)) multiplexer_4 (
    .in0(shifter_2_out[3:0]), .in1(or_3_out), .out(multiplexer_4_out[3:0]), .sel(or_4_out));  // open: en
  Shifter shifter_3 (.in(multiplexer_4_out), .\dist (3'b001), .out(shifter_3_out));
  Comparator #(.width(4), .mode("unsigned")) comparator_3 (
    .a(shifter_3_out[7:4]), .b(d), .gt(comparator_3_gt), .eq(comparator_3_eq));  // open: lt
  Subtractor #(.width(4)) subtractor_3 (.a(shifter_3_out[7:4]), .b(d), .out(subtractor_3_out));  // open: bin, bout
  assign or_5_out = shifter_3_out[3:0] | 4'b0001;  // OR_Gate or_5, 4 bits wide
  or or_6 (or_6_out, comparator_3_gt, comparator_3_eq);
  Multiplexer #(.width(4)) multiplexer_5 (
    .in0(shifter_3_out[7:4]), .in1(subtractor_3_out), .out(multiplexer_5_out), .sel(or_6_out));  // open: en
  Multiplexer #(.width(4)) multiplexer_6 (
    .in0(shifter_3_out[3:0]), .in1(or_5_out), .out(multiplexer_6_out), .sel(or_6_out));  // open: en
  Shifter shifter_4 (.in({multiplexer_5_out, multiplexer_6_out}), .\dist (3'b001), .out(shifter_4_out));
  Comparator #(.width(4), .mode("unsigned")) comparator_4 (
    .a(shifter_4_out[7:4]), .b(d), .gt(comparator_4_gt), .eq(comparator_4_eq));  // open: lt
  Subtractor #(.width(4)) subtractor_4 (.a(shifter_4_out[7:4]), .b(d), .out(subtractor_4_out));  // open: bin, bout
  assign or_7_out = shifter_4_out[3:0] | 4'b0001;  // OR_Gate or_7, 4 bits wide
  or or_8 (or_8_out, comparator_4_gt, comparator_4_eq);
  Multiplexer #(.width(4)) multiplexer_7 (
    .in0(shifter_4_out[7:4]), .in1(subtractor_4_out), .out(rem), .sel(or_8_out));  // open: en
  Multiplexer #(.width(4)) multiplexer_8 (
    .in0(shifter_4_out[3:0]), .in1(or_7_out), .out(quot), .sel(or_8_out));  // open: en
  // Probe on quot
  // Probe on rem
  // OR_Gate or_9 is placed but not wired
endmodule

module DIV1 (
  input  [31:0] n1,
  input  [31:0] n2,
  input  [31:0] d,
  output [31:0] n1o,
  output [31:0] n2o
);

  wire comparator_1_eq, comparator_1_gt, or_3_out;
  wire [31:0] and_1_out, or_1_out, or_2_out, shifter_1_out, shifter_2_out, shifter_3_out, subtractor_1_out;

  assign and_1_out = n2 & 32'h80000000;  // AND_Gate and_1, 32 bits wide
  Shifter #(.width(32)) shifter_1 (.in(n2), .\dist (5'b00001), .out(shifter_1_out));
  Shifter #(.width(32)) shifter_2 (.in(n1), .\dist (5'b00001), .out(shifter_2_out));
  Shifter #(.width(32), .shift("lr")) shifter_3 (.in(and_1_out), .\dist ({5{1'b1}}), .out(shifter_3_out));
  assign or_1_out = shifter_2_out | shifter_3_out;  // OR_Gate or_1, 32 bits wide
  Comparator #(.width(32), .mode("unsigned")) comparator_1 (
    .a(or_1_out), .b(d), .gt(comparator_1_gt), .eq(comparator_1_eq));  // open: lt
  Subtractor #(.width(32)) subtractor_1 (.a(or_1_out), .b(d), .out(subtractor_1_out));  // open: bin, bout
  assign or_2_out = shifter_1_out | 32'h1;  // OR_Gate or_2, 32 bits wide
  or or_3 (or_3_out, comparator_1_gt, comparator_1_eq);
  Multiplexer #(.width(32)) multiplexer_1 (
    .in0(or_1_out), .in1(subtractor_1_out), .out(n1o), .sel(or_3_out));  // open: en
  Multiplexer #(.width(32)) multiplexer_2 (.in0(shifter_1_out), .in1(or_2_out), .out(n2o), .sel(or_3_out));  // open: en
endmodule

module \_32位除法器  (
  input  [31:0] n_31_0,
  input  [31:0] d_31_0,
  output [31:0] quot_31_0,
  output [31:0] rem_31_0
);

  wire [31:0] div1_1_n1o, div1_1_n2o, div1_3_n1o, div1_3_n2o, div1_4_n1o, div1_4_n2o, div1_5_n1o, div1_5_n2o,
       div1_6_n1o, div1_6_n2o, div1_7_n1o, div1_7_n2o, div1_8_n1o, div1_8_n2o, div1_9_n1o, div1_9_n2o,
       div1_10_n1o, div1_10_n2o, div1_11_n1o, div1_11_n2o, div1_12_n1o, div1_12_n2o, div1_13_n1o,
       div1_13_n2o, div1_14_n1o, div1_14_n2o, div1_15_n1o, div1_15_n2o, div1_16_n1o, div1_16_n2o,
       div1_17_n1o, div1_17_n2o, div1_18_n1o, div1_18_n2o, div1_19_n1o, div1_19_n2o, div1_20_n1o,
       div1_20_n2o, div1_21_n1o, div1_21_n2o, div1_22_n1o, div1_22_n2o, div1_23_n1o, div1_23_n2o,
       div1_24_n1o, div1_24_n2o, div1_25_n1o, div1_25_n2o, div1_26_n1o, div1_26_n2o, div1_27_n1o,
       div1_27_n2o, div1_28_n1o, div1_28_n2o, div1_29_n1o, div1_29_n2o, div1_30_n1o, div1_30_n2o,
       div1_31_n1o, div1_31_n2o, div1_32_n1o, div1_32_n2o;

  // Probe on n_31_0
  // Probe on d_31_0
  DIV1 div1_1 (.n1(div1_4_n1o), .n2(div1_4_n2o), .d(d_31_0), .n1o(div1_1_n1o), .n2o(div1_1_n2o));
  DIV1 div1_2 (.n1(div1_6_n1o), .n2(div1_6_n2o), .d(d_31_0), .n1o(rem_31_0), .n2o(quot_31_0));
  // Probe on quot_31_0
  DIV1 div1_3 (.n1({32{1'b0}}), .n2(n_31_0), .d(d_31_0), .n1o(div1_3_n1o), .n2o(div1_3_n2o));
  DIV1 div1_4 (.n1(div1_8_n1o), .n2(div1_8_n2o), .d(d_31_0), .n1o(div1_4_n1o), .n2o(div1_4_n2o));
  DIV1 div1_5 (.n1(div1_1_n1o), .n2(div1_1_n2o), .d(d_31_0), .n1o(div1_5_n1o), .n2o(div1_5_n2o));
  DIV1 div1_6 (.n1(div1_10_n1o), .n2(div1_10_n2o), .d(d_31_0), .n1o(div1_6_n1o), .n2o(div1_6_n2o));
  // Probe on rem_31_0
  DIV1 div1_7 (.n1(div1_3_n1o), .n2(div1_3_n2o), .d(d_31_0), .n1o(div1_7_n1o), .n2o(div1_7_n2o));
  DIV1 div1_8 (.n1(div1_12_n1o), .n2(div1_12_n2o), .d(d_31_0), .n1o(div1_8_n1o), .n2o(div1_8_n2o));
  DIV1 div1_9 (.n1(div1_5_n1o), .n2(div1_5_n2o), .d(d_31_0), .n1o(div1_9_n1o), .n2o(div1_9_n2o));
  DIV1 div1_10 (.n1(div1_14_n1o), .n2(div1_14_n2o), .d(d_31_0), .n1o(div1_10_n1o), .n2o(div1_10_n2o));
  DIV1 div1_11 (.n1(div1_7_n1o), .n2(div1_7_n2o), .d(d_31_0), .n1o(div1_11_n1o), .n2o(div1_11_n2o));
  DIV1 div1_12 (.n1(div1_16_n1o), .n2(div1_16_n2o), .d(d_31_0), .n1o(div1_12_n1o), .n2o(div1_12_n2o));
  DIV1 div1_13 (.n1(div1_9_n1o), .n2(div1_9_n2o), .d(d_31_0), .n1o(div1_13_n1o), .n2o(div1_13_n2o));
  DIV1 div1_14 (.n1(div1_18_n1o), .n2(div1_18_n2o), .d(d_31_0), .n1o(div1_14_n1o), .n2o(div1_14_n2o));
  DIV1 div1_15 (.n1(div1_11_n1o), .n2(div1_11_n2o), .d(d_31_0), .n1o(div1_15_n1o), .n2o(div1_15_n2o));
  DIV1 div1_16 (.n1(div1_22_n1o), .n2(div1_22_n2o), .d(d_31_0), .n1o(div1_16_n1o), .n2o(div1_16_n2o));
  DIV1 div1_17 (.n1(div1_13_n1o), .n2(div1_13_n2o), .d(d_31_0), .n1o(div1_17_n1o), .n2o(div1_17_n2o));
  DIV1 div1_18 (.n1(div1_21_n1o), .n2(div1_21_n2o), .d(d_31_0), .n1o(div1_18_n1o), .n2o(div1_18_n2o));
  DIV1 div1_19 (.n1(div1_15_n1o), .n2(div1_15_n2o), .d(d_31_0), .n1o(div1_19_n1o), .n2o(div1_19_n2o));
  DIV1 div1_20 (.n1(div1_17_n1o), .n2(div1_17_n2o), .d(d_31_0), .n1o(div1_20_n1o), .n2o(div1_20_n2o));
  DIV1 div1_21 (.n1(div1_26_n1o), .n2(div1_26_n2o), .d(d_31_0), .n1o(div1_21_n1o), .n2o(div1_21_n2o));
  DIV1 div1_22 (.n1(div1_25_n1o), .n2(div1_25_n2o), .d(d_31_0), .n1o(div1_22_n1o), .n2o(div1_22_n2o));
  DIV1 div1_23 (.n1(div1_19_n1o), .n2(div1_19_n2o), .d(d_31_0), .n1o(div1_23_n1o), .n2o(div1_23_n2o));
  DIV1 div1_24 (.n1(div1_20_n1o), .n2(div1_20_n2o), .d(d_31_0), .n1o(div1_24_n1o), .n2o(div1_24_n2o));
  DIV1 div1_25 (.n1(div1_29_n1o), .n2(div1_29_n2o), .d(d_31_0), .n1o(div1_25_n1o), .n2o(div1_25_n2o));
  DIV1 div1_26 (.n1(div1_30_n1o), .n2(div1_30_n2o), .d(d_31_0), .n1o(div1_26_n1o), .n2o(div1_26_n2o));
  DIV1 div1_27 (.n1(div1_23_n1o), .n2(div1_23_n2o), .d(d_31_0), .n1o(div1_27_n1o), .n2o(div1_27_n2o));
  DIV1 div1_28 (.n1(div1_24_n1o), .n2(div1_24_n2o), .d(d_31_0), .n1o(div1_28_n1o), .n2o(div1_28_n2o));
  DIV1 div1_29 (.n1(div1_31_n1o), .n2(div1_31_n2o), .d(d_31_0), .n1o(div1_29_n1o), .n2o(div1_29_n2o));
  DIV1 div1_30 (.n1(div1_32_n1o), .n2(div1_32_n2o), .d(d_31_0), .n1o(div1_30_n1o), .n2o(div1_30_n2o));
  DIV1 div1_31 (.n1(div1_27_n1o), .n2(div1_27_n2o), .d(d_31_0), .n1o(div1_31_n1o), .n2o(div1_31_n2o));
  DIV1 div1_32 (.n1(div1_28_n1o), .n2(div1_28_n2o), .d(d_31_0), .n1o(div1_32_n1o), .n2o(div1_32_n2o));
endmodule
