// Logisim project 电子钟.circ as structural Verilog: 18 circuits, main circuit 带置位功能的四位二进制可逆计数器
module \带置位功能的四位二进制可逆计数器  (
  input  CPD,
  input  CPU,
  input  CLR,
  input  SD,
  input  SC,
  input  SB,
  input  SA,
  output QD,
  output QC,
  output QB,
  output QA
);

  wire and_1_out, and_2_out, and_3_out, and_4_out, and_5_out, and_6_out, d_ff_1_qn, d_ff_2_qn, d_ff_3_qn,
       d_ff_4_qn, or_1_out, or_2_out, or_3_out, or_4_out;

  and and_1 (and_1_out, d_ff_2_qn, d_ff_3_qn, d_ff_4_qn, CPD);
  and and_2 (and_2_out, QC, QB, QA, CPU);
  and and_3 (and_3_out, d_ff_3_qn, d_ff_4_qn, CPD);
  and and_4 (and_4_out, QB, QA, CPU);
  and and_5 (and_5_out, d_ff_4_qn, CPD);
  and and_6 (and_6_out, QA, CPU);
  or or_1 (or_1_out, and_1_out, SD, and_2_out);
  or or_2 (or_2_out, and_3_out, SC, and_4_out);
  or or_3 (or_3_out, and_5_out, SB, and_6_out);
  or or_4 (or_4_out, CPD, SA, CPU);
  D_Flip_Flop #(.trigger("falling")) d_ff_1 (
    .clk(or_1_out), .D(d_ff_1_qn), .Q(QD), .Qn(d_ff_1_qn), .reset(CLR));  // open: preset, en
  D_Flip_Flop #(.trigger("falling")) d_ff_2 (
    .clk(or_2_out), .D(d_ff_2_qn), .Q(QC), .Qn(d_ff_2_qn), .reset(CLR));  // open: preset, en
  D_Flip_Flop #(.trigger("falling")) d_ff_3 (
    .clk(or_3_out), .D(d_ff_3_qn), .Q(QB), .Qn(d_ff_3_qn), .reset(CLR));  // open: preset, en
  D_Flip_Flop #(.trigger("falling")) d_ff_4 (
    .clk(or_4_out), .D(d_ff_4_qn), .Q(QA), .Qn(d_ff_4_qn), .reset(CLR));  // open: preset, en
endmodule

module \模10计数器  (
  input  CPU,
  input  CLR,
  input  CPD,
  output QD,
  output QC,
  output QB,
  output QA,
  output borrow,
  output carry
);

  wire and_1_out, buffer_1_out, buffer_2_out, buffer_3_out, buffer_4_out, nor_1_out, not_1_out, or_1_out;

  buf buffer_1 (buffer_1_out, CPD);
  buf buffer_2 (buffer_2_out, buffer_3_out);
  buf buffer_3 (buffer_3_out, buffer_1_out);
  not not_1 (not_1_out, borrow);
  buf buffer_4 (buffer_4_out, CPD);
  or or_1 (or_1_out, CLR, carry);
  and and_1 (and_1_out, buffer_2_out, not_1_out);
  \带置位功能的四位二进制可逆计数器  \u_带置位功能的四位二进制可逆计数器_1  (
    .QD(QD), .CPD(and_1_out), .QC(QC), .CPU(CPU), .QB(QB), .QA(QA), .CLR(or_1_out), .SD(borrow), .SC(1'b0),
    .SB(1'b0), .SA(borrow));
  nor nor_1 (nor_1_out, QD, QC, QB, QA);
  and and_2 (borrow, buffer_4_out, nor_1_out);
  and and_3 (carry, QD, QB);
endmodule

module \模6计数器  (
  input  CPU,
  input  CLR,
  input  CPD,
  output out_4,
  output out_5,
  output out_6,
  output out_7,
  output borrow,
  output carry
);

  wire and_1_out, buffer_1_out, buffer_2_out, buffer_3_out, buffer_4_out, nor_1_out, not_1_out, or_1_out;

  buf buffer_1 (buffer_1_out, CPD);
  buf buffer_2 (buffer_2_out, buffer_3_out);
  buf buffer_3 (buffer_3_out, buffer_1_out);
  not not_1 (not_1_out, borrow);
  buf buffer_4 (buffer_4_out, CPD);
  or or_1 (or_1_out, CLR, carry);
  and and_1 (and_1_out, buffer_2_out, not_1_out);
  \带置位功能的四位二进制可逆计数器  \u_带置位功能的四位二进制可逆计数器_1  (
    .QD(out_4), .CPD(and_1_out), .QC(out_5), .CPU(CPU), .QB(out_6), .QA(out_7), .CLR(or_1_out), .SD(1'b0),
    .SC(borrow), .SB(1'b0), .SA(borrow));
  nor nor_1 (nor_1_out, out_4, out_5, out_6, out_7);
  and and_2 (borrow, buffer_4_out, nor_1_out);
  and and_3 (carry, out_5, out_6);
endmodule

module \模60计数器  (
  input  CPU,
  input  CPD,
  input  Adj,
  input  Clr,
  output Q0d,
  output Q0c,
  output Q0b,
  output Q0a,
  output Q1d,
  output Q1c,
  output Q1b,
  output Q1a,
  output nQcc
);

  wire multiplexer_1_out, \模6计数器_1_carry , \模10计数器_1_borrow , \模10计数器_1_carry ;

  Multiplexer multiplexer_1 (.in0(1'b0), .in1(CPD), .out(multiplexer_1_out), .sel(Adj));  // open: en
  \模10计数器  \u_模10计数器_1  (
    .CPU(CPU), .CLR(Clr), .CPD(multiplexer_1_out), .borrow(\模10计数器_1_borrow ), .carry(\模10计数器_1_carry ),
    .QD(Q0d), .QC(Q0c), .QB(Q0b), .QA(Q0a));
  \模6计数器  \u_模6计数器_1  (
    .CPU(\模10计数器_1_carry ), .CLR(Clr), .CPD(\模10计数器_1_borrow ), .carry(\模6计数器_1_carry ), .out_4(Q1d),
    .out_5(Q1c), .out_6(Q1b), .out_7(Q1a));  // open: borrow
  not not_1 (nQcc, \模6计数器_1_carry );
endmodule

module \_60进制测试  (
  input  in_1,
  input  in_2,
  input  in_3,
  input  in_4,
  output out_5
);

  wire [3:0] \模60计数器_1_q0a , \模60计数器_1_q1a ;

  \模60计数器  \u_模60计数器_1  (
    .CPU(in_1), .CPD(in_3), .Adj(in_2), .Clr(in_4), .nQcc(out_5), .Q0d(\模60计数器_1_q0a [3]),
    .Q0b(\模60计数器_1_q0a [1]), .Q0a(\模60计数器_1_q0a [0]), .Q1d(\模60计数器_1_q1a [3]), .Q1c(\模60计数器_1_q1a [2]),
    .Q1b(\模60计数器_1_q1a [1]), .Q1a(\模60计数器_1_q1a [0]), .Q0c(\模60计数器_1_q0a [2]));
  Hex_Digit_Display hex_digit_display_1 (.value(\模60计数器_1_q1a ));  // open: dp
  Hex_Digit_Display hex_digit_display_2 (.value(\模60计数器_1_q0a ));  // open: dp
endmodule

module \模4计数器  (
  input  CPU,
  input  CLR,
  input  CPD,
  output out_4,
  output out_5,
  output out_6,
  output out_7,
  output borrow,
  output carry
);

  wire and_1_out, buffer_1_out, buffer_2_out, buffer_3_out, buffer_4_out, nor_1_out, not_1_out, or_1_out;

  buf buffer_1 (buffer_1_out, CPD);
  buf buffer_2 (buffer_2_out, buffer_3_out);
  buf buffer_3 (buffer_3_out, buffer_1_out);
  not not_1 (not_1_out, borrow);
  buf buffer_4 (buffer_4_out, CPD);
  or or_1 (or_1_out, CLR, carry);
  and and_1 (and_1_out, buffer_2_out, not_1_out);
  \带置位功能的四位二进制可逆计数器  \u_带置位功能的四位二进制可逆计数器_1  (
    .QD(out_4), .CPD(and_1_out), .QC(carry), .CPU(CPU), .QB(out_6), .QA(out_7), .CLR(or_1_out), .SD(1'b0),
    .SC(1'b0), .SB(borrow), .SA(borrow));
  nor nor_1 (nor_1_out, out_4, carry, out_6, out_7);
  and and_2 (borrow, buffer_4_out, nor_1_out);

  assign out_5 = carry;
endmodule

module \小于24的二进制转十进制  (
  input  in_1,
  input  in_2,
  input  in_3,
  input  in_4,
  input  in_5,
  input  in_6,
  input  in_7,
  input  in_8,
  output out_9,
  output out_10,
  output out_11,
  output out_12,
  output out_13,
  output out_14,
  output out_15,
  output out_16
);

  wire multiplexer_2_out, multiplexer_3_out, nand_1_out, \二进制转8421码_1_t0 , \先行进位的加法器_1_s0 , \先行进位的加法器_1_s1 ,
       \先行进位的加法器_1_s2 , \先行进位的加法器_1_s3 ;

  nand nand_1 (nand_1_out, in_8, \二进制转8421码_1_t0 );
  and and_1 (out_11, in_8, \二进制转8421码_1_t0 );
  \二进制转8421码  \u_二进制转8421码_1  (
    .A3(\先行进位的加法器_1_s3 ), .A2(\先行进位的加法器_1_s2 ), .A1(\先行进位的加法器_1_s1 ), .A0(\先行进位的加法器_1_s0 ),
    .T0(\二进制转8421码_1_t0 ), .S3(out_13), .S2(out_14), .S1(out_15), .S0(out_16));  // open: T3, T2, T1
  Multiplexer multiplexer_1 (.in0(\二进制转8421码_1_t0 ), .in1(nand_1_out), .out(out_12), .sel(in_8));  // open: en
  \先行进位的加法器  \u_先行进位的加法器_1  (
    .C0(1'b0), .A0(in_7), .B0(1'b0), .A1(in_6), .B1(multiplexer_3_out), .A2(in_5), .B2(multiplexer_2_out),
    .A3(in_4), .B3(1'b0), .S0(\先行进位的加法器_1_s0 ), .S1(\先行进位的加法器_1_s1 ), .S2(\先行进位的加法器_1_s2 ),
    .S3(\先行进位的加法器_1_s3 ));  // open: C4
  Multiplexer multiplexer_2 (.in0(1'b0), .in1(1'b1), .out(multiplexer_2_out), .sel(in_8));  // open: en
  Multiplexer multiplexer_3 (.in0(1'b0), .in1(1'b1), .out(multiplexer_3_out), .sel(in_8));  // open: en

  assign out_9 = 1'b0;
  assign out_10 = 1'b0;
endmodule

module \选择模12或模24计数器  (
  input  CPu,
  input  CPd,
  input  Adj,
  input  Clr,
  input  Set,
  output out_6,
  output out_7,
  output out_8,
  output out_9,
  output out_10,
  output out_11,
  output out_12,
  output out_13,
  output \上午下午控制 ,
  output \借位 
);

  wire comparator_1_eq, comparator_1_gt, multiplexer_1_out, not_1_out, or_1_out, \模4计数器_1_borrow ,
       \模4计数器_1_carry , \模6计数器_1_carry ;
  wire [3:0] \模4计数器_1_out_7 , \模6计数器_1_out_7 ;
  wire [7:0] adder_1_out, multiplexer_2_out, \n4x4乘法器_1_p_7_0 , subtractor_1_out;

  Multiplexer multiplexer_1 (.in0(1'b0), .in1(CPd), .out(multiplexer_1_out), .sel(Adj));  // open: en
  \模4计数器  \u_模4计数器_1  (
    .CPU(CPu), .CLR(Clr), .CPD(multiplexer_1_out), .borrow(\模4计数器_1_borrow ), .carry(\模4计数器_1_carry ),
    .out_4(\模4计数器_1_out_7 [3]), .out_5(\模4计数器_1_out_7 [2]), .out_6(\模4计数器_1_out_7 [1]),
    .out_7(\模4计数器_1_out_7 [0]));
  not not_1 (not_1_out, Set);
  Adder adder_1 (.a(\n4x4乘法器_1_p_7_0 ), .b({4'b0000, \模4计数器_1_out_7 }), .out(adder_1_out));  // open: cin, cout
  Comparator #(.mode("unsigned")) comparator_1 (
    .a(adder_1_out), .b(8'hc), .gt(comparator_1_gt), .eq(comparator_1_eq));  // open: lt
  \模6计数器  \u_模6计数器_1  (
    .CPU(\模4计数器_1_carry ), .CLR(Clr), .CPD(\模4计数器_1_borrow ), .carry(\模6计数器_1_carry ),
    .out_4(\模6计数器_1_out_7 [3]), .out_5(\模6计数器_1_out_7 [2]), .out_6(\模6计数器_1_out_7 [1]),
    .out_7(\模6计数器_1_out_7 [0]));  // open: borrow
  or or_1 (or_1_out, comparator_1_gt, comparator_1_eq);
  and and_1 (\上午下午控制 , or_1_out, not_1_out);
  \_4x4乘法器  \u_4x4乘法器_1  (.a_3_0(4'b0100), .b_3_0(\模6计数器_1_out_7 ), .p_7_0(\n4x4乘法器_1_p_7_0 ));
  not not_2 (\借位 , \模6计数器_1_carry );
  Subtractor subtractor_1 (.a(adder_1_out), .b(8'hc), .out(subtractor_1_out));  // open: bin, bout
  Multiplexer #(.width(8)) multiplexer_2 (
    .in0(adder_1_out), .in1(subtractor_1_out), .out(multiplexer_2_out), .sel(\上午下午控制 ));  // open: en
  \小于24的二进制转十进制  \u_小于24的二进制转十进制_1  (
    .in_8(multiplexer_2_out[4]), .out_9(out_6), .out_10(out_7), .out_11(out_8), .out_12(out_9),
    .out_13(out_10), .out_14(out_11), .out_15(out_12), .out_16(out_13), .in_1(multiplexer_2_out[7]),
    .in_2(multiplexer_2_out[6]), .in_3(multiplexer_2_out[5]), .in_4(multiplexer_2_out[3]),
    .in_5(multiplexer_2_out[2]), .in_6(multiplexer_2_out[1]), .in_7(multiplexer_2_out[0]));
endmodule

module \模12或模24检测电路  (
  input  in_1,
  input  in_2,
  input  in_3,
  input  in_4,
  input  in_5,
  output out_6,
  output out_7
);

  wire [3:0] \选择模12或模24计数器_1_out_9 , \选择模12或模24计数器_1_out_13 ;

  Hex_Digit_Display hex_digit_display_1 (.value(\选择模12或模24计数器_1_out_9 ));  // open: dp
  \选择模12或模24计数器  \u_选择模12或模24计数器_1  (
    .CPu(in_1), .CPd(in_3), .Adj(in_2), .Clr(in_5), .\借位 (out_6), .Set(in_4), .\上午下午控制 (out_7),
    .out_6(\选择模12或模24计数器_1_out_9 [3]), .out_7(\选择模12或模24计数器_1_out_9 [2]), .out_8(\选择模12或模24计数器_1_out_9 [1]),
    .out_12(\选择模12或模24计数器_1_out_13 [1]), .out_13(\选择模12或模24计数器_1_out_13 [0]),
    .out_9(\选择模12或模24计数器_1_out_9 [0]), .out_10(\选择模12或模24计数器_1_out_13 [3]),
    .out_11(\选择模12或模24计数器_1_out_13 [2]));
  Hex_Digit_Display hex_digit_display_2 (.value(\选择模12或模24计数器_1_out_13 ));  // open: dp
endmodule

module \显示上午和下午电路  (
  input  AM_FM,
  input  TT,
  output [4:0] _1,
  output [4:0] _2,
  output [4:0] _3,
  output [4:0] _4
);

  wire [4:0] multiplexer_1_out, multiplexer_2_out, multiplexer_3_out;

  Multiplexer #(.width(5)) multiplexer_1 (
    .in0(5'b00001), .in1(5'b10000), .out(multiplexer_1_out), .sel(AM_FM));  // open: en
  Multiplexer #(.width(5)) multiplexer_2 (
    .in0(5'b00101), .in1(5'b10100), .out(multiplexer_2_out), .sel(AM_FM));  // open: en
  Multiplexer #(.width(5)) multiplexer_3 (
    .in0({5{1'b0}}), .in1({5{1'b1}}), .out(multiplexer_3_out), .sel(TT));  // open: en
  assign _1 = multiplexer_1_out & multiplexer_3_out;  // AND_Gate and_1, 5 bits wide
  assign _2 = {5{1'b1}} & multiplexer_3_out;  // AND_Gate and_2, 5 bits wide
  assign _3 = multiplexer_2_out & multiplexer_3_out;  // AND_Gate and_3, 5 bits wide

  assign _4 = _1;
endmodule

module \上午下午显示检测电路  (
  input  in_1,
  input  in_2
);

  wire [4:0] \显示上午和下午电路_1__1 , \显示上午和下午电路_1__2 , \显示上午和下午电路_1__3 , \显示上午和下午电路_1__4 ;

  \显示上午和下午电路  \u_显示上午和下午电路_1  (
    .AM_FM(in_1), .TT(in_2), ._1(\显示上午和下午电路_1__1 ), ._2(\显示上午和下午电路_1__2 ), ._3(\显示上午和下午电路_1__3 ),
    ._4(\显示上午和下午电路_1__4 ));
  DotMatrix #(.matrixcols(4), .matrixrows(5)) dotmatrix_1 (
    .col0(\显示上午和下午电路_1__1 ), .col1(\显示上午和下午电路_1__2 ), .col2(\显示上午和下午电路_1__3 ), .col3(\显示上午和下午电路_1__4 ));
endmodule

module \整点报时  (
  input  \分钟1 ,
  input  \分钟2 ,
  input  \分钟3 ,
  input  \分钟4 ,
  input  \秒1 ,
  input  \秒2 ,
  input  \震荡源 ,
  output \输出脉冲 
);

  and and_1 (\输出脉冲 , \分钟1 , \分钟2 , \分钟3 , \分钟4 , \秒1 , \秒2 , \震荡源 );
endmodule

module \整点报时测试  (
  input  in_1,
  input  in_2,
  input  in_3,
  input  in_4,
  input  in_5,
  input  in_6,
  output out_7
);

  wire button_1_out;

  \整点报时  \u_整点报时_1  (
    .\分钟1 (in_1), .\分钟2 (in_2), .\分钟3 (in_3), .\分钟4 (in_4), .\秒1 (in_5), .\秒2 (in_6), .\震荡源 (button_1_out),
    .\输出脉冲 (out_7));
  Button button_1 (.out(button_1_out));
endmodule

module \秒计时脉冲产生电路  (
  input  \输入 ,
  output \输出 
);

  wire t_ff_1_q, t_ff_2_q;

  T_Flip_Flop #(.trigger("falling")) t_ff_1 (.clk(\输入 ), .T(1'b1), .Q(t_ff_1_q));  // open: Qn, preset, reset, en
  T_Flip_Flop #(.trigger("falling")) t_ff_2 (.clk(t_ff_1_q), .T(1'b1), .Q(t_ff_2_q));  // open: Qn, preset, reset, en
  T_Flip_Flop #(.trigger("falling")) t_ff_3 (.clk(t_ff_2_q), .T(1'b1), .Q(\输出 ));  // open: Qn, preset, reset, en
endmodule

module \闹钟  (
  input  [3:0] \当前秒1 ,
  input  [3:0] \当前秒2 ,
  input  [3:0] \输入分 ,
  input  [3:0] \当前分 ,
  input  [3:0] \输入分_2 ,
  input  [3:0] \当前分_2 ,
  input  [3:0] \输入时 ,
  input  [3:0] \当前时 ,
  input  [3:0] \输入时_2 ,
  input  [3:0] \当前时_2 ,
  input  \_12_24模式 ,
  input  \输入脉冲 ,
  input  \是否启闹 ,
  input  \上午_下午 ,
  output \电子钟输出 
);

  wire and_1_out, and_2_out, and_3_out, and_4_out, and_5_out, comparator_1_eq, comparator_2_eq,
       comparator_2_gt, comparator_3_lt, comparator_4_eq, comparator_5_eq, comparator_6_eq, comparator_7_eq,
       comparator_7_gt, comparator_8_eq, comparator_8_gt, comparator_9_eq, comparator_9_lt, comparator_10_eq,
       comparator_11_eq, not_1_out, or_1_out, or_2_out, or_3_out, or_4_out, or_5_out;
  wire [3:0] adder_1_out, multiplexer_1_out, multiplexer_2_out, multiplexer_3_out, multiplexer_4_out,
       subtractor_1_out, subtractor_2_out, subtractor_3_out;

  not not_1 (not_1_out, \_12_24模式 );
  and and_1 (and_1_out, not_1_out, \上午_下午 );
  Comparator #(.width(4), .mode("unsigned")) comparator_1 (
    .a(\当前秒1 ), .b(4'b0000), .eq(comparator_1_eq));  // open: gt, lt
  Comparator #(.width(4), .mode("unsigned")) comparator_2 (
    .a(\当前秒2 ), .b(4'b0000), .gt(comparator_2_gt), .eq(comparator_2_eq));  // open: lt
  Comparator #(.width(4), .mode("unsigned")) comparator_3 (
    .a(\当前秒2 ), .b(4'b1010), .lt(comparator_3_lt));  // open: gt, eq
  Comparator #(.width(4), .mode("unsigned")) comparator_4 (.a(\输入分 ), .b(\当前分 ), .eq(comparator_4_eq));  // open: gt, lt
  Comparator #(.width(4), .mode("unsigned")) comparator_5 (
    .a(\输入分_2 ), .b(\当前分_2 ), .eq(comparator_5_eq));  // open: gt, lt
  Multiplexer #(.width(4)) multiplexer_1 (
    .in0(\输入时 ), .in1(multiplexer_3_out), .out(multiplexer_1_out), .sel(and_1_out));  // open: en
  Multiplexer #(.width(4)) multiplexer_2 (
    .in0(\输入时_2 ), .in1(multiplexer_4_out), .out(multiplexer_2_out), .sel(and_1_out));  // open: en
  Comparator #(.width(4), .mode("unsigned")) comparator_6 (
    .a(\输入时 ), .b(4'b0010), .eq(comparator_6_eq));  // open: gt, lt
  Comparator #(.width(4), .mode("unsigned")) comparator_7 (
    .a(\输入时_2 ), .b(4'b0010), .gt(comparator_7_gt), .eq(comparator_7_eq));  // open: lt
  Comparator #(.width(4), .mode("unsigned")) comparator_8 (
    .a(\输入时 ), .b(4'b0001), .gt(comparator_8_gt), .eq(comparator_8_eq));  // open: lt
  Comparator #(.width(4), .mode("unsigned")) comparator_9 (
    .a(\输入时_2 ), .b(4'b1001), .eq(comparator_9_eq), .lt(comparator_9_lt));  // open: gt
  Comparator #(.width(4), .mode("unsigned")) comparator_10 (
    .a(multiplexer_1_out), .b(\当前时 ), .eq(comparator_10_eq));  // open: gt, lt
  Comparator #(.width(4), .mode("unsigned")) comparator_11 (
    .a(multiplexer_2_out), .b(\当前时_2 ), .eq(comparator_11_eq));  // open: gt, lt
  or or_1 (or_1_out, comparator_7_gt, comparator_7_eq);
  or or_2 (or_2_out, comparator_8_gt, comparator_8_eq);
  or or_3 (or_3_out, comparator_9_eq, comparator_9_lt);
  or or_4 (or_4_out, comparator_2_gt, comparator_2_eq);
  and and_2 (and_2_out, comparator_6_eq, or_1_out);
  and and_3 (and_3_out, or_1_out, or_2_out);
  and and_4 (and_4_out, comparator_8_eq, or_3_out);
  Subtractor #(.width(4)) subtractor_1 (.a(\输入时 ), .b(4'b0001), .out(subtractor_1_out));  // open: bin, bout
  Subtractor #(.width(4)) subtractor_2 (.a(\输入时_2 ), .b(4'b0010), .out(subtractor_2_out));  // open: bin, bout
  Subtractor #(.width(4)) subtractor_3 (.a(\输入时 ), .b(4'b0010), .out(subtractor_3_out));  // open: bin, bout
  Adder #(.width(4)) adder_1 (.a(\输入时_2 ), .b(4'b1000), .out(adder_1_out));  // open: cin, cout
  and and_5 (and_5_out, and_3_out, and_4_out);
  or or_5 (or_5_out, and_2_out, and_5_out);
  and and_6 (\电子钟输出 , comparator_1_eq, or_4_out, comparator_3_lt, comparator_4_eq, comparator_5_eq, comparator_10_eq, comparator_11_eq, \输入脉冲 , \是否启闹 );
  Multiplexer #(.width(4)) multiplexer_3 (
    .in0(subtractor_3_out), .in1(subtractor_1_out), .out(multiplexer_3_out), .sel(or_5_out));  // open: en
  Multiplexer #(.width(4)) multiplexer_4 (
    .in0(adder_1_out), .in1(subtractor_2_out), .out(multiplexer_4_out), .sel(or_5_out));  // open: en
endmodule

module \闹钟测试  (
  input  in_1,
  input  in_2,
  input  in_3,
  input  [3:0] in_4,
  input  [3:0] in_5,
  input  [3:0] in_6,
  input  [3:0] in_7,
  input  [3:0] in_8,
  input  [3:0] in_9,
  input  [3:0] in_10,
  input  [3:0] in_11,
  input  [3:0] in_12,
  input  [3:0] in_13,
  output out_14
);

  wire button_1_out;

  Button button_1 (.out(button_1_out));
  \闹钟  \u_闹钟_1  (
    .\当前秒2 (in_5), .\输入分 (in_6), .\当前分 (in_7), .\输入时_2 (in_12), .\当前时_2 (in_13), .\输入脉冲 (button_1_out),
    .\是否启闹 (in_1), .\当前秒1 (in_4), .\输入分_2 (in_8), .\当前分_2 (in_9), .\输入时 (in_10), .\当前时 (in_11),
    .\电子钟输出 (out_14), .\_12_24模式 (in_2), .\上午_下午 (in_3));
endmodule

module \多功能数字电子钟  (
  input  ALRAM,
  input  [3:0] \输入分1 ,
  input  [3:0] \输入分2 ,
  input  [3:0] \输入时1 ,
  input  [3:0] \输入时2 ,
  input  SET,
  input  CPu,
  input  CPd,
  input  Adj0,
  input  Adj1,
  input  Clr,
  input  \_8hz信号 ,
  output [4:0] out_13,
  output [4:0] out_14,
  output [4:0] out_15,
  output [4:0] out_16,
  output \闹钟 ,
  output \定点报时 ,
  output [3:0] out_19,
  output [3:0] out_20,
  output [3:0] out_21,
  output [3:0] out_22,
  output [3:0] out_23,
  output [3:0] out_24
);

  wire multiplexer_1_out, multiplexer_2_out, multiplexer_3_out, multiplexer_4_out, not_1_out, not_2_out,
       not_3_out, or_1_out, or_2_out, \模60计数器_1_nqcc , \模60计数器_2_nqcc , \秒计时脉冲产生电路_1_输出 ,
       \选择模12或模24计数器_1_上午下午控制 ;

  \闹钟  \u_闹钟_1  (
    .\当前秒2 (out_22), .\输入分 (\输入分1 ), .\当前分 (out_23), .\输入时_2 (\输入时2 ), .\当前时_2 (out_20),
    .\输入脉冲 (\秒计时脉冲产生电路_1_输出 ), .\是否启闹 (ALRAM), .\当前秒1 (out_21), .\输入分_2 (\输入分2 ), .\当前分_2 (out_24),
    .\输入时 (\输入时1 ), .\当前时 (out_19), .\电子钟输出 (\闹钟 ), .\_12_24模式 (SET), .\上午_下午 (\选择模12或模24计数器_1_上午下午控制 ));
  \秒计时脉冲产生电路  \u_秒计时脉冲产生电路_1  (.\输入 (\_8hz信号 ), .\输出 (\秒计时脉冲产生电路_1_输出 ));
  \模60计数器  \u_模60计数器_1  (
    .CPU(\秒计时脉冲产生电路_1_输出 ), .CPD(1'b0), .Adj(1'b0), .Clr(Clr), .nQcc(\模60计数器_1_nqcc ), .Q0d(out_22[3]),
    .Q0b(out_22[1]), .Q0a(out_22[0]), .Q1d(out_21[3]), .Q1c(out_21[2]), .Q1b(out_21[1]), .Q1a(out_21[0]),
    .Q0c(out_22[2]));
  Multiplexer multiplexer_1 (.in0(1'b0), .in1(CPu), .out(multiplexer_1_out), .sel(Adj1));  // open: en
  Multiplexer multiplexer_2 (.in0(1'b0), .in1(CPu), .out(multiplexer_2_out), .sel(Adj0));  // open: en
  Multiplexer multiplexer_3 (.in0(1'b0), .in1(CPd), .out(multiplexer_3_out), .sel(Adj1));  // open: en
  Multiplexer multiplexer_4 (.in0(1'b0), .in1(CPd), .out(multiplexer_4_out), .sel(Adj0));  // open: en
  \整点报时  \u_整点报时_1  (
    .\分钟1 (out_23[0]), .\分钟2 (out_23[2]), .\分钟3 (out_24[3]), .\分钟4 (out_24[0]), .\秒1 (out_21[2]),
    .\秒2 (out_21[0]), .\震荡源 (\秒计时脉冲产生电路_1_输出 ), .\输出脉冲 (\定点报时 ));
  not not_1 (not_1_out, \模60计数器_1_nqcc );
  or or_1 (or_1_out, multiplexer_1_out, not_1_out);
  \模60计数器  \u_模60计数器_2  (
    .CPU(or_1_out), .CPD(multiplexer_3_out), .Adj(Adj1), .Clr(Clr), .nQcc(\模60计数器_2_nqcc ), .Q0d(out_24[3]),
    .Q0b(out_24[1]), .Q0a(out_24[0]), .Q1d(out_23[3]), .Q1c(out_23[2]), .Q1b(out_23[1]), .Q1a(out_23[0]),
    .Q0c(out_24[2]));
  \显示上午和下午电路  \u_显示上午和下午电路_1  (
    .AM_FM(\选择模12或模24计数器_1_上午下午控制 ), .TT(not_2_out), ._1(out_13), ._2(out_14), ._3(out_15), ._4(out_16));
  not not_2 (not_2_out, SET);
  not not_3 (not_3_out, \模60计数器_2_nqcc );
  or or_2 (or_2_out, multiplexer_2_out, not_3_out);
  \选择模12或模24计数器  \u_选择模12或模24计数器_1  (
    .CPu(or_2_out), .CPd(multiplexer_4_out), .Adj(Adj0), .Clr(Clr), .Set(SET),
    .\上午下午控制 (\选择模12或模24计数器_1_上午下午控制 ), .out_6(out_19[3]), .out_7(out_19[2]), .out_8(out_19[1]),
    .out_12(out_20[1]), .out_13(out_20[0]), .out_9(out_19[0]), .out_10(out_20[3]), .out_11(out_20[2]));  // open: 借位
endmodule

module \多功能数字钟测试电路  (
  input  in_1,
  input  in_2,
  input  in_3,
  input  in_4,
  input  in_5,
  input  in_6,
  input  in_7,
  input  [3:0] in_8,
  input  [3:0] in_9,
  input  [3:0] in_10,
  input  [3:0] in_11
);

  wire clock_1_out, \多功能数字电子钟_1_定点报时 , \多功能数字电子钟_1_闹钟 ;
  wire [3:0] \多功能数字电子钟_1_out_19 , \多功能数字电子钟_1_out_20 , \多功能数字电子钟_1_out_21 , \多功能数字电子钟_1_out_22 ,
       \多功能数字电子钟_1_out_23 , \多功能数字电子钟_1_out_24 ;
  wire [4:0] \多功能数字电子钟_1_out_13 , \多功能数字电子钟_1_out_14 , \多功能数字电子钟_1_out_15 , \多功能数字电子钟_1_out_16 ;

  Clock clock_1 (.out(clock_1_out));
  DotMatrix #(.matrixcols(4), .matrixrows(5)) dotmatrix_1 (
    .col0(\多功能数字电子钟_1_out_13 ), .col1(\多功能数字电子钟_1_out_14 ), .col2(\多功能数字电子钟_1_out_15 ),
    .col3(\多功能数字电子钟_1_out_16 ));
  Hex_Digit_Display hex_digit_display_1 (.value(\多功能数字电子钟_1_out_19 ));  // open: dp
  Hex_Digit_Display hex_digit_display_2 (.value(\多功能数字电子钟_1_out_20 ));  // open: dp
  \多功能数字电子钟  \u_多功能数字电子钟_1  (
    .ALRAM(in_1), .\输入分1 (in_8), .\输入分2 (in_9), .\输入时1 (in_10), .\输入时2 (in_11), .SET(in_6), .CPu(in_4),
    .CPd(in_5), .Adj0(in_2), .Adj1(in_3), .Clr(in_7), .\闹钟 (\多功能数字电子钟_1_闹钟 ), .out_21(\多功能数字电子钟_1_out_21 ),
    .out_22(\多功能数字电子钟_1_out_22 ), .\定点报时 (\多功能数字电子钟_1_定点报时 ), .out_23(\多功能数字电子钟_1_out_23 ),
    .out_13(\多功能数字电子钟_1_out_13 ), .out_24(\多功能数字电子钟_1_out_24 ), .out_14(\多功能数字电子钟_1_out_14 ),
    .out_15(\多功能数字电子钟_1_out_15 ), .out_16(\多功能数字电子钟_1_out_16 ), .out_19(\多功能数字电子钟_1_out_19 ),
    .out_20(\多功能数字电子钟_1_out_20 ), .\_8hz信号 (clock_1_out));
  Hex_Digit_Display hex_digit_display_3 (.value(\多功能数字电子钟_1_out_23 ));  // open: dp
  Hex_Digit_Display hex_digit_display_4 (.value(\多功能数字电子钟_1_out_21 ));  // open: dp
  Hex_Digit_Display hex_digit_display_5 (.value(\多功能数字电子钟_1_out_24 ));  // open: dp
  Hex_Digit_Display hex_digit_display_6 (.value(\多功能数字电子钟_1_out_22 ));  // open: dp
  LED led_1 (.in(\多功能数字电子钟_1_定点报时 ));
  LED led_2 (.in(\多功能数字电子钟_1_闹钟 ));
  Hex_Digit_Display hex_digit_display_7 (.value(in_10));  // open: dp
  Hex_Digit_Display hex_digit_display_8 (.value(in_11));  // open: dp
  Hex_Digit_Display hex_digit_display_9 (.value(in_9));  // open: dp
  Hex_Digit_Display hex_digit_display_10 (.value(in_8));  // open: dp
endmodule
