// Logisim project fibonacci.circ as structural Verilog: 6 circuits, main circuit sqrX
module sqrX (
  input  [31:0] a,
  input  [31:0] b,
  input  [31:0] c,
  input  [31:0] d,
  output [31:0] a_prime,
  output [31:0] b_prime,
  output [31:0] c_prime,
  output [31:0] d_prime
);

  wire [31:0] multiplier_1_out, multiplier_2_out, multiplier_3_out, multiplier_4_out, multiplier_5_out,
       multiplier_6_out, multiplier_7_out, multiplier_8_out;

  Multiplier #(.width(32)) multiplier_1 (.a(a), .b(a), .out(multiplier_1_out));  // open: cin, cout
  Multiplier #(.width(32)) multiplier_2 (.a(b), .b(c), .out(multiplier_2_out));  // open: cin, cout
  Multiplier #(.width(32)) multiplier_3 (.a(a), .b(b), .out(multiplier_3_out));  // open: cin, cout
  Multiplier #(.width(32)) multiplier_4 (.a(b), .b(d), .out(multiplier_4_out));  // open: cin, cout
  Multiplier #(.width(32)) multiplier_5 (.a(a), .b(c), .out(multiplier_5_out));  // open: cin, cout
  Multiplier #(.width(32)) multiplier_6 (.a(d), .b(c), .out(multiplier_6_out));  // open: cin, cout
  Multiplier #(.width(32)) multiplier_7 (.a(b), .b(c), .out(multiplier_7_out));  // open: cin, cout
  Multiplier #(.width(32)) multiplier_8 (.a(d), .b(d), .out(multiplier_8_out));  // open: cin, cout
  Adder #(.width(32)) adder_1 (.a(multiplier_1_out), .b(multiplier_2_out), .out(a_prime));  // open: cin, cout
  Adder #(.width(32)) adder_2 (.a(multiplier_3_out), .b(multiplier_4_out), .out(b_prime));  // open: cin, cout
  Adder #(.width(32)) adder_3 (.a(multiplier_5_out), .b(multiplier_6_out), .out(c_prime));  // open: cin, cout
  Adder #(.width(32)) adder_4 (.a(multiplier_7_out), .b(multiplier_8_out), .out(d_prime));  // open: cin, cout
endmodule

module sqrX_A (
  input  [31:0] a,
  input  [31:0] b,
  input  [31:0] c,
  input  [31:0] d,
  output [31:0] a_prime_prime,
  output [31:0] b_prime_prime,
  output [31:0] c_prime_prime,
  output [31:0] d_prime_prime
);

  wire [31:0] adder_2_out, adder_3_out, adder_5_out, adder_6_out, multiplier_1_out, multiplier_2_out,
       multiplier_3_out, multiplier_4_out, multiplier_5_out, multiplier_6_out, multiplier_7_out;

  Multiplier #(.width(32)) multiplier_1 (.a(a), .b(a), .out(multiplier_1_out));  // open: cin, cout
  Multiplier #(.width(32)) multiplier_2 (.a(a), .b(b), .out(multiplier_2_out));  // open: cin, cout
  Multiplier #(.width(32)) multiplier_3 (.a(a), .b(c), .out(multiplier_3_out));  // open: cin, cout
  Multiplier #(.width(32)) multiplier_4 (.a(b), .b(c), .out(multiplier_4_out));  // open: cin, cout
  Multiplier #(.width(32)) multiplier_5 (.a(d), .b(b), .out(multiplier_5_out));  // open: cin, cout
  Multiplier #(.width(32)) multiplier_6 (.a(b), .b(d), .out(multiplier_6_out));  // open: cin, cout
  Multiplier #(.width(32)) multiplier_7 (.a(d), .b(d), .out(multiplier_7_out));  // open: cin, cout
  Adder #(.width(32)) adder_1 (.a(multiplier_2_out), .b(multiplier_5_out), .out(a_prime_prime));  // open: cin, cout
  Adder #(.width(32)) adder_2 (.a(multiplier_1_out), .b(multiplier_4_out), .out(adder_2_out));  // open: cin, cout
  Adder #(.width(32)) adder_3 (.a(multiplier_2_out), .b(multiplier_5_out), .out(adder_3_out));  // open: cin, cout
  Adder #(.width(32)) adder_4 (.a(multiplier_4_out), .b(multiplier_7_out), .out(c_prime_prime));  // open: cin, cout
  Adder #(.width(32)) adder_5 (.a(multiplier_6_out), .b(multiplier_3_out), .out(adder_5_out));  // open: cin, cout
  Adder #(.width(32)) adder_6 (.a(multiplier_7_out), .b(multiplier_4_out), .out(adder_6_out));  // open: cin, cout
  Adder #(.width(32)) adder_7 (.a(adder_2_out), .b(adder_3_out), .out(b_prime_prime));  // open: cin, cout
  Adder #(.width(32)) adder_8 (.a(adder_5_out), .b(adder_6_out), .out(d_prime_prime));  // open: cin, cout
endmodule

// Fi
module Fibo (
  input  start,
  input  clr,
  input  clk,
  input  ni_1,
  output [31:0] Fi
);

  wire or_1_out;
  wire [31:0] multiplexer_1_out, multiplexer_2_out, multiplexer_3_out, multiplexer_4_out, multiplexer_5_out,
       multiplexer_6_out, multiplexer_7_out, multiplexer_8_out, register_1_q, register_3_q, register_4_q,
       sqrx_1_a_prime, sqrx_1_b_prime, sqrx_1_c_prime, sqrx_1_d_prime, sqrx_a_1_a_prime_prime,
       sqrx_a_1_b_prime_prime, sqrx_a_1_c_prime_prime, sqrx_a_1_d_prime_prime;

  or or_1 (or_1_out, clr, clk);
  Multiplexer #(.width(32)) multiplexer_1 (
    .in0({32{1'b0}}), .in1(multiplexer_5_out), .out(multiplexer_1_out), .sel(start));  // open: en
  Multiplexer #(.width(32)) multiplexer_2 (
    .in0(32'h1), .in1(multiplexer_6_out), .out(multiplexer_2_out), .sel(start));  // open: en
  Multiplexer #(.width(32)) multiplexer_3 (
    .in0(32'h1), .in1(multiplexer_7_out), .out(multiplexer_3_out), .sel(start));  // open: en
  Multiplexer #(.width(32)) multiplexer_4 (
    .in0(32'h1), .in1(multiplexer_8_out), .out(multiplexer_4_out), .sel(start));  // open: en
  Register #(.width(32)) register_1 (.D(multiplexer_1_out), .Q(register_1_q), .clk(or_1_out));  // open: en, clr
  Register #(.width(32)) register_2 (.D(multiplexer_2_out), .Q(Fi), .clk(or_1_out));  // open: en, clr
  Register #(.width(32)) register_3 (.D(multiplexer_3_out), .Q(register_3_q), .clk(or_1_out));  // open: en, clr
  Register #(.width(32)) register_4 (.D(multiplexer_4_out), .Q(register_4_q), .clk(or_1_out));  // open: en, clr
  sqrX sqrx_1 (
    .a(register_1_q), .b(Fi), .c(register_3_q), .d(register_4_q), .a_prime(sqrx_1_a_prime),
    .b_prime(sqrx_1_b_prime), .c_prime(sqrx_1_c_prime), .d_prime(sqrx_1_d_prime));
  sqrX_A sqrx_a_1 (
    .a(register_1_q), .b(Fi), .c(register_3_q), .d(register_4_q), .a_prime_prime(sqrx_a_1_a_prime_prime),
    .b_prime_prime(sqrx_a_1_b_prime_prime), .c_prime_prime(sqrx_a_1_c_prime_prime),
    .d_prime_prime(sqrx_a_1_d_prime_prime));
  Multiplexer #(.width(32)) multiplexer_5 (
    .in0(sqrx_1_a_prime), .in1(sqrx_a_1_a_prime_prime), .out(multiplexer_5_out), .sel(ni_1));  // open: en
  Multiplexer #(.width(32)) multiplexer_6 (
    .in0(sqrx_1_b_prime), .in1(sqrx_a_1_b_prime_prime), .out(multiplexer_6_out), .sel(ni_1));  // open: en
  Multiplexer #(.width(32)) multiplexer_7 (
    .in0(sqrx_1_c_prime), .in1(sqrx_a_1_c_prime_prime), .out(multiplexer_7_out), .sel(ni_1));  // open: en
  Multiplexer #(.width(32)) multiplexer_8 (
    .in0(sqrx_1_d_prime), .in1(sqrx_a_1_d_prime_prime), .out(multiplexer_8_out), .sel(ni_1));  // open: en
endmodule

module Display (
  input  [31:0] F_n,
  output [3:0] D0,
  output [3:0] D1,
  output [3:0] D2,
  output [3:0] D3,
  output [3:0] D4,
  output [3:0] D5,
  output [3:0] D6,
  output [3:0] D7,
  output [3:0] D8,
  output [3:0] D9
);

  wire [31:0] divider_1_out, divider_2_out, divider_3_out, divider_4_out, divider_5_out, divider_6_out,
       divider_7_out, divider_8_out;
  wire [31:4] divider_1_rem, divider_2_rem, divider_3_rem, divider_4_rem, divider_5_rem, divider_6_rem,
       divider_7_rem, divider_8_rem, divider_9_out, divider_9_rem;

  Divider #(.width(32)) divider_1 (.a(F_n), .b(32'ha), .out(divider_1_out), .rem({divider_1_rem, D0}));  // open: upper
  Divider #(.width(32)) divider_2 (
    .a(divider_1_out), .b(32'ha), .out(divider_2_out), .rem({divider_2_rem, D1}));  // open: upper
  Divider #(.width(32)) divider_3 (
    .a(divider_2_out), .b(32'ha), .out(divider_3_out), .rem({divider_3_rem, D2}));  // open: upper
  Divider #(.width(32)) divider_4 (
    .a(divider_3_out), .b(32'ha), .out(divider_4_out), .rem({divider_4_rem, D3}));  // open: upper
  Divider #(.width(32)) divider_5 (
    .a(divider_4_out), .b(32'ha), .out(divider_5_out), .rem({divider_5_rem, D4}));  // open: upper
  Divider #(.width(32)) divider_6 (
    .a(divider_5_out), .b(32'ha), .out(divider_6_out), .rem({divider_6_rem, D5}));  // open: upper
  Divider #(.width(32)) divider_7 (
    .a(divider_6_out), .b(32'ha), .out(divider_7_out), .rem({divider_7_rem, D6}));  // open: upper
  Divider #(.width(32)) divider_8 (
    .a(divider_7_out), .b(32'ha), .out(divider_8_out), .rem({divider_8_rem, D7}));  // open: upper
  Divider #(.width(32)) divider_9 (
    .a(divider_8_out), .b(32'ha), .out({divider_9_out, D9}), .rem({divider_9_rem, D8}));  // open: upper
endmodule

module Controller (
  input  [5:0] n,
  input  clear,
  input  clock,
  output clear_2,
  output ni_1,
  output start,
  output clock_2
);

  wire and_1_out, and_2_out, buffer_1_out, buffer_2_out, buffer_3_out, buffer_4_out, buffer_5_out,
       buffer_6_out, buffer_7_out, buffer_8_out, buffer_9_out, buffer_10_out, buffer_11_out, comparator_1_eq,
       comparator_1_lt, d_ff_1_q, or_1_out, or_2_out, or_3_out, or_4_out;
  wire [7:0] counter_1_q;

  Counter #(.max('h7), .ongoal("stay")) counter_1 (
    .count(1'b1), .Q(counter_1_q), .clk(clock), .clr(clear));  // open: load, D, carry
  buf buffer_1 (buffer_1_out, buffer_2_out);
  buf buffer_2 (buffer_2_out, buffer_3_out);
  buf buffer_3 (buffer_3_out, clear);
  Comparator comparator_1 (.a(counter_1_q), .b(8'h5), .eq(comparator_1_eq), .lt(comparator_1_lt));  // open: gt
  buf buffer_4 (buffer_4_out, buffer_5_out);
  buf buffer_5 (buffer_5_out, buffer_1_out);
  buf buffer_6 (buffer_6_out, buffer_4_out);
  or or_1 (or_1_out, comparator_1_eq, comparator_1_lt);
  buf buffer_7 (buffer_7_out, buffer_8_out);
  buf buffer_8 (buffer_8_out, buffer_6_out);
  and and_1 (and_1_out, comparator_1_lt, clock);
  buf buffer_9 (buffer_9_out, buffer_11_out);
  buf buffer_10 (buffer_10_out, buffer_7_out);
  buf buffer_11 (buffer_11_out, buffer_10_out);
  Shift_Register #(.length(6)) shift_register_1 (
    .clk(or_2_out), .out(ni_1), .load(clear), .d0(n[0]), .d1(n[1]), .d2(n[2]), .d3(n[3]), .d4(n[4]), .d5(n[5]));  // open: shift, in, clr, q0, q1, q2, q3, q4, q5
  or or_2 (or_2_out, and_1_out, clear);
  and and_2 (and_2_out, or_1_out, clock);
  buf buffer_12 (clear_2, buffer_9_out);
  or or_3 (or_3_out, ni_1, d_ff_1_q);
  D_Flip_Flop #(.trigger("falling")) d_ff_1 (
    .clk(or_2_out), .D(or_3_out), .Q(d_ff_1_q), .reset(clear));  // open: Qn, preset, en
  or or_4 (or_4_out, ni_1, d_ff_1_q);
  and and_3 (clock_2, d_ff_1_q, and_2_out);
  D_Flip_Flop d_ff_2 (.clk(or_2_out), .D(or_4_out), .Q(start), .reset(clear));  // open: Qn, preset, en
endmodule

module main (
  input  [5:0] n
);

  wire clear_out, clk_out, controller_1_clear_2, controller_1_clock_2, controller_1_ni_1, controller_1_start;
  wire [3:0] display_1_d0, display_1_d1, display_1_d2, display_1_d3, display_1_d4, display_1_d5,
       display_1_d6, display_1_d7, display_1_d8, display_1_d9;
  wire [31:0] fibo_1_fi;

  Button clear (.out(clear_out));
  Button clk (.out(clk_out));
  Controller controller_1 (
    .n(n), .clear(clear_out), .clear_2(controller_1_clear_2), .ni_1(controller_1_ni_1),
    .clock_2(controller_1_clock_2), .clock(clk_out), .start(controller_1_start));
  Fibo fibo_1 (
    .start(controller_1_start), .clr(controller_1_clear_2), .clk(controller_1_clock_2), .Fi(fibo_1_fi),
    .ni_1(controller_1_ni_1));
  Hex_Digit_Display hex_digit_display_1 (.value(display_1_d9));  // open: dp
  Hex_Digit_Display hex_digit_display_2 (.value(display_1_d7));  // open: dp
  Hex_Digit_Display hex_digit_display_3 (.value(display_1_d8));  // open: dp
  Display display_1 (
    .F_n(fibo_1_fi), .D0(display_1_d0), .D1(display_1_d1), .D2(display_1_d2), .D3(display_1_d3),
    .D4(display_1_d4), .D5(display_1_d5), .D6(display_1_d6), .D7(display_1_d7), .D8(display_1_d8),
    .D9(display_1_d9));
  Hex_Digit_Display hex_digit_display_4 (.value(display_1_d6));  // open: dp
  Hex_Digit_Display hex_digit_display_5 (.value(display_1_d5));  // open: dp
  Hex_Digit_Display hex_digit_display_6 (.value(display_1_d4));  // open: dp
  Hex_Digit_Display hex_digit_display_7 (.value(display_1_d3));  // open: dp
  Hex_Digit_Display hex_digit_display_8 (.value(display_1_d2));  // open: dp
  Hex_Digit_Display hex_digit_display_9 (.value(display_1_d1));  // open: dp
  Hex_Digit_Display hex_digit_display_10 (.value(display_1_d0));  // open: dp
endmodule
